# Fritzing sketch Device Access Box sketch (saved by Fritzing 1.0.1rc)
breadboards: 1

parts:
  Part1 = RFID-RC522-v2
  LED2 = smd LED [color="Red (633nm)" package="0805 [SMD]"]
  WeMos_D1_Mini1 = WeMos D1 Mini
  R1 = Resistor [tolerance=±5% resistance=150 package="0603 [SMD]"]
  LED6 = LED - 3mm [color="Green (555nm)" current=0.030 package="3 mm [THT]"]
  R2 = Resistor [tolerance=±5% resistance=150 package="0603 [SMD]"]
  IC1 = DIP - 6 pins [chip_label="5V RELAY" package="DIP (Dual Inline) [THT]"]

nets:
  N1: Part1.SDA, WeMos_D1_Mini1.D8
  N2: Part1.SCK, WeMos_D1_Mini1.D5
  N3: Part1.MOSI, WeMos_D1_Mini1.D7
  N4: Part1.MISO, WeMos_D1_Mini1.D6
  N5: Part1.GND, LED2.cathode, WeMos_D1_Mini1.G, LED6.cathode, IC1.DC-
  N6: Part1.RST, WeMos_D1_Mini1.D3
  N7: Part1.3_3V, WeMos_D1_Mini1.3V3, IC1.DC+
  N8: WeMos_D1_Mini1.D0, IC1.IN
  N9: WeMos_D1_Mini1.D2, R2.Pin_0
  N10: WeMos_D1_Mini1.D4, R1.Pin_0

notes:
  RFID reader wiring
  SDA D8
  SCL(SCK) D5
  MOSI D7
  MISO D6
  IRQ -
  GND gnd
  RST D3
  3.3v 3.3v
  GND running thru top line
  3.3V thru 2nd line
  AC power in
  AC Power Out
  5v Power Adapter
  150 Ohm Resistor
  In - "COM"
  Out - "NO"

custom parts:
  RFID-RC522-v2: A simple China made RFID-RC522 Reader; do check the pin labels, as this is a MFRC522 based clone.
  DIP - 6 pins: A DIP stand-in part for whatever IC you want. With 6 pins on a 300mil dual inline package (DIP) footprint.
