# Fritzing sketch Signin Box wiring diagram (saved by Fritzing 0.9.10b)
breadboards: 1

parts:
  WeMos_D1_Mini2 = WeMos D1 Mini
  Part2 = RFID-RC522-v2
  LED7 = smd LED [color="Red (633nm)" package="0805 [SMD]"]
  R3 = Resistor [tolerance=±5% resistance=150 package="0603 [SMD]"]
  R4 = Resistor [tolerance=±5% resistance=150 package="0603 [SMD]"]
  LED8 = LED - 3mm [color="Green (555nm)" current=0.030 package="3 mm [THT]"]
  J1 = Piezo Speaker
  R5 = Resistor [tolerance=±5% resistance=100 package="0603 [SMD]"]

nets:
  N1: WeMos_D1_Mini2.3V3, Part2.3_3V
  N2: WeMos_D1_Mini2.D1, R5.Pin_0
  N3: WeMos_D1_Mini2.D2, R3.Pin_0
  N4: WeMos_D1_Mini2.D3, Part2.RST
  N5: WeMos_D1_Mini2.D4, R4.Pin_0
  N6: WeMos_D1_Mini2.D5, Part2.SCK
  N7: WeMos_D1_Mini2.D6, Part2.MISO
  N8: WeMos_D1_Mini2.D7, Part2.MOSI
  N9: WeMos_D1_Mini2.D8, Part2.SDA
  N10: Part2.GND, LED7.cathode, LED8.cathode, J1.pin1

notes:
  RFID reader wiring
  SDA D8
  SCL(SCK) D5
  MOSI D7
  MISO D6
  IRQ -
  GND gnd
  RST D3
  3.3v 3.3v

custom parts:
  RFID-RC522-v2: A simple China made RFID-RC522 Reader; do check the pin labels, as this is a MFRC522 based clone.
